# Fritzing sketch Schema (saved by Fritzing 0.9.3b)
breadboards: 1

parts:
  Part1 = Arduino Uno (Rev3)
  DHT11 = Humidity and Temperature Sensor RHT03
  R1 = Resistor [tolerance=±5% resistance=4.7k package=THT]
  Q1 = NPN-Transistor [package="TO92 [THT]"]
  M1 = DC Motor
  R2 = Resistor [tolerance=±5% resistance=220 package=THT]

nets:
  N1: Part1.D11_PWM/MOSI, R2.Pin_1
  N2: Part1.D2, DHT11.Data-signal, R1.Pin_1
  5V: Part1.5V, DHT11.Vcc, R1.Pin_0
  N3: Part1.GND, DHT11.GND_2, M1.pin_1
  N4: Part1.VIN, Q1.E
  N5: Q1.B, R2.Pin_0
  N6: Q1.C, M1.pin_2
